# Fritzing sketch sketch_dispositivo (saved by Fritzing 0.9.3b)
breadboards: 1

parts:
  DHT1 = DHT22 Humidity and Temperature Sensor
  SHT35-D1 = SHT35-D [package="SIP (Single Inline) [THT]"]
  A1 = SIM7600G-H
  M1 = ESP32-S3-DevKitC-1-N8R8-v1 [part_number=ESP32-S3-DevKitC-1-N8R8-v1]

nets:
  VDD: DHT1.VDD, SHT35-D1.VDD, M1.pin_1, M1.pin_2
  N1: DHT1.DATA, M1.pin_39
  GND: DHT1.GND, SHT35-D1.GND, A1.Pin_2, A1.Pin_7, M1.pin_22, M1.pin_23, M1.pin_24, M1.pin_44
  N2: SHT35-D1.SCL, M1.pin_18
  N3: SHT35-D1.SDA, M1.pin_17
  N4: A1.Pin_3, M1.pin_43
  N5: A1.Pin_4, M1.pin_42
  N6: A1.Pin_5, M1.pin_21
  N7: A1.Pin_6, M1.pin_38

custom parts:
  SHT35-D: SHT35-D is an I2C connected temperature and humidity sensor
  SIM7600G-H: Sim7600g Breakout Board, Mini Sim7600g-h Cat4 Kits with Gps 4g antenna.
  ESP32-S3-DevKitC-1-N8R8-v1: ESP32-S3-DevKitC-1-N8R8-v1 This module is 44pins long (2x22) and 11 pins width.
